// Logisim project 2107020_Clock.circ as structural Verilog: 6 circuits, main circuit main
module main (
  input  Skip_On_off,
  input  MSB,
  input  Preset,
  input  in_4,
  input  Preset_2,
  input  Preset_3,
  input  in_7,
  input  LSB,
  input  MSB_2,
  input  in_10,
  input  in_11,
  input  LSB_2
);

  wire and_1_out, and_2_out, and_3_out, and_5_out, and_6_out, and_8_out, and_9_out, bcd_to_7_segment_1_a_2,
       bcd_to_7_segment_1_b_2, bcd_to_7_segment_1_c_2, bcd_to_7_segment_1_d_2, bcd_to_7_segment_1_e,
       bcd_to_7_segment_1_f, bcd_to_7_segment_1_g, bcd_to_7_segment_2_a_2, bcd_to_7_segment_2_b_2,
       bcd_to_7_segment_2_c_2, bcd_to_7_segment_2_d_2, bcd_to_7_segment_2_e, bcd_to_7_segment_2_f,
       bcd_to_7_segment_2_g, bcd_to_7_segment_3_a_2, bcd_to_7_segment_3_b_2, bcd_to_7_segment_3_c_2,
       bcd_to_7_segment_3_d_2, bcd_to_7_segment_3_e, bcd_to_7_segment_3_f, bcd_to_7_segment_3_g,
       bcd_to_7_segment_4_a_2, bcd_to_7_segment_4_b_2, bcd_to_7_segment_4_c_2, bcd_to_7_segment_4_d_2,
       bcd_to_7_segment_4_e, bcd_to_7_segment_4_f, bcd_to_7_segment_4_g, bcd_to_7_segment_5_a_2,
       bcd_to_7_segment_5_b_2, bcd_to_7_segment_5_c_2, bcd_to_7_segment_5_d_2, bcd_to_7_segment_5_e,
       bcd_to_7_segment_5_f, bcd_to_7_segment_5_g, bcd_to_7_segment_6_a_2, bcd_to_7_segment_6_b_2,
       bcd_to_7_segment_6_c_2, bcd_to_7_segment_6_d_2, bcd_to_7_segment_6_e, bcd_to_7_segment_6_f,
       bcd_to_7_segment_6_g, Clk_from_MIN, Clk_from_SEC, clock_1_out, n4_bit_comparator_1_a___b_3,
       n4_bit_comparator_2_a___b_3, n4_bit_comparator_3_a___b_3, n4_bit_comparator_4_a___b_3,
       n4_bit_comparator_5_a___b_3, n4_bit_comparator_6_a___b_3, or_1_out, or_2_out, or_3_out, or_4_out,
       Q0_0, Q0_1, Q0_2, Q0_3, Q0_4, Q0_5, Q1_0, Q1_1, Q1_2, Q1_3, Q1_4, Q1_5, Q2_0, Q2_1, Q2_2, Q2_3, Q2_4,
       Q2_5, Q3_0, Q3_1, Q3_2, Q3_3, Q3_4, Q3_5;

  _4_bit_up_counter u_4_bit_up_counter_1 (
    .Clock(or_2_out), .CLR(or_1_out), .Q3(Q3_5), .Q2(Q2_5), .Q1(Q1_5), .Q0(Q0_5));  // open: Preset
  or or_1 (or_1_out, and_1_out, and_3_out);
  _7_Segment_Display u_7_segment_display_1 (
    .g(bcd_to_7_segment_1_g), .f(bcd_to_7_segment_1_f), .a(bcd_to_7_segment_1_a_2),
    .b(bcd_to_7_segment_1_b_2), .e(bcd_to_7_segment_1_e), .d(bcd_to_7_segment_1_d_2),
    .c(bcd_to_7_segment_1_c_2));  // open: dp
  BCD_to_7_segment bcd_to_7_segment_1 (
    .A(Q3_5), .B(Q2_5), .C(Q1_5), .D(Q0_5), .a_2(bcd_to_7_segment_1_a_2), .b_2(bcd_to_7_segment_1_b_2),
    .c_2(bcd_to_7_segment_1_c_2), .d_2(bcd_to_7_segment_1_d_2), .e(bcd_to_7_segment_1_e),
    .f(bcd_to_7_segment_1_f), .g(bcd_to_7_segment_1_g));
  and and_1 (and_1_out, Q1_5, Q3_5);
  or or_2 (or_2_out, and_2_out, and_3_out);
  and and_2 (and_2_out, Q3_4, Q1_4);
  _4_bit_up_counter u_4_bit_up_counter_2 (
    .Clock(Clk_from_MIN), .CLR(or_2_out), .Preset(Preset_2), .Q3(Q3_4), .Q2(Q2_4), .Q1(Q1_4), .Q0(Q0_4));
  _7_Segment_Display u_7_segment_display_2 (
    .g(bcd_to_7_segment_2_g), .f(bcd_to_7_segment_2_f), .a(bcd_to_7_segment_2_a_2),
    .b(bcd_to_7_segment_2_b_2), .e(bcd_to_7_segment_2_e), .d(bcd_to_7_segment_2_d_2),
    .c(bcd_to_7_segment_2_c_2));  // open: dp
  BCD_to_7_segment bcd_to_7_segment_2 (
    .A(Q3_4), .B(Q2_4), .C(Q1_4), .D(Q0_4), .a_2(bcd_to_7_segment_2_a_2), .b_2(bcd_to_7_segment_2_b_2),
    .c_2(bcd_to_7_segment_2_c_2), .d_2(bcd_to_7_segment_2_d_2), .e(bcd_to_7_segment_2_e),
    .f(bcd_to_7_segment_2_f), .g(bcd_to_7_segment_2_g));
  _4_bit_Comparator u_4_bit_comparator_1 (
    .A3(Q3_5), .A2(Q2_5), .A1(Q1_5), .A0(Q0_5), .B3(MSB), .B2(in_4), .B1(in_7), .B0(LSB),
    .A___B_3(n4_bit_comparator_1_a___b_3));  // open: A___B, A___B_2
  _4_bit_Comparator u_4_bit_comparator_2 (
    .A3(Q3_4), .A2(Q2_4), .A1(Q1_4), .A0(Q0_4), .B3(MSB_2), .B2(in_10), .B1(in_11), .B0(LSB_2),
    .A___B_3(n4_bit_comparator_2_a___b_3));  // open: A___B, A___B_2
  and and_3 (and_3_out, n4_bit_comparator_1_a___b_3, Skip_On_off, n4_bit_comparator_2_a___b_3);
  _4_bit_up_counter u_4_bit_up_counter_3 (
    .Clock(or_3_out), .CLR(Clk_from_MIN), .Q3(Q3_3), .Q2(Q1_3), .Q1(Q2_3), .Q0(Q0_3));  // open: Preset
  and and_4 (Clk_from_MIN, Q2_3, Q1_3);
  _7_Segment_Display u_7_segment_display_3 (
    .g(bcd_to_7_segment_3_g), .f(bcd_to_7_segment_3_f), .a(bcd_to_7_segment_3_a_2),
    .b(bcd_to_7_segment_3_b_2), .e(bcd_to_7_segment_3_e), .d(bcd_to_7_segment_3_d_2),
    .c(bcd_to_7_segment_3_c_2));  // open: dp
  BCD_to_7_segment bcd_to_7_segment_3 (
    .A(Q3_3), .B(Q1_3), .C(Q2_3), .D(Q0_3), .a_2(bcd_to_7_segment_3_a_2), .b_2(bcd_to_7_segment_3_b_2),
    .c_2(bcd_to_7_segment_3_c_2), .d_2(bcd_to_7_segment_3_d_2), .e(bcd_to_7_segment_3_e),
    .f(bcd_to_7_segment_3_f), .g(bcd_to_7_segment_3_g));
  or or_3 (or_3_out, and_5_out, and_6_out);
  and and_5 (and_5_out, Q3_2, Q1_2);
  _7_Segment_Display u_7_segment_display_4 (
    .g(bcd_to_7_segment_4_g), .f(bcd_to_7_segment_4_f), .a(bcd_to_7_segment_4_a_2),
    .b(bcd_to_7_segment_4_b_2), .e(bcd_to_7_segment_4_e), .d(bcd_to_7_segment_4_d_2),
    .c(bcd_to_7_segment_4_c_2));  // open: dp
  BCD_to_7_segment bcd_to_7_segment_4 (
    .A(Q3_2), .B(Q2_2), .C(Q1_2), .D(Q0_2), .a_2(bcd_to_7_segment_4_a_2), .b_2(bcd_to_7_segment_4_b_2),
    .c_2(bcd_to_7_segment_4_c_2), .d_2(bcd_to_7_segment_4_d_2), .e(bcd_to_7_segment_4_e),
    .f(bcd_to_7_segment_4_f), .g(bcd_to_7_segment_4_g));
  _4_bit_up_counter u_4_bit_up_counter_4 (
    .Clock(Clk_from_SEC), .CLR(or_3_out), .Preset(Preset), .Q3(Q3_2), .Q2(Q2_2), .Q1(Q1_2), .Q0(Q0_2));
  _4_bit_Comparator u_4_bit_comparator_3 (
    .A3(Q3_3), .A2(Q2_3), .A1(Q1_3), .A0(Q0_3), .B3(1'b0), .B2(1'b0), .B1(1'b0), .B0(1'b1),
    .A___B_3(n4_bit_comparator_3_a___b_3));  // open: A___B, A___B_2
  _4_bit_Comparator u_4_bit_comparator_4 (
    .A3(Q3_2), .A2(Q2_2), .A1(Q1_2), .A0(Q0_2), .B3(1'b1), .B2(1'b0), .B1(1'b0), .B0(1'b1),
    .A___B_3(n4_bit_comparator_4_a___b_3));  // open: A___B, A___B_2
  and and_6 (and_6_out, n4_bit_comparator_3_a___b_3, n4_bit_comparator_4_a___b_3);
  _4_bit_up_counter u_4_bit_up_counter_5 (
    .Clock(or_4_out), .CLR(Clk_from_SEC), .Q3(Q3_1), .Q2(Q2_1), .Q1(Q1_1), .Q0(Q0_1));  // open: Preset
  and and_7 (Clk_from_SEC, Q1_1, Q2_1);
  _7_Segment_Display u_7_segment_display_5 (
    .g(bcd_to_7_segment_5_g), .f(bcd_to_7_segment_5_f), .a(bcd_to_7_segment_5_a_2),
    .b(bcd_to_7_segment_5_b_2), .e(bcd_to_7_segment_5_e), .d(bcd_to_7_segment_5_d_2),
    .c(bcd_to_7_segment_5_c_2));  // open: dp
  BCD_to_7_segment bcd_to_7_segment_5 (
    .A(Q3_1), .B(Q2_1), .C(Q1_1), .D(Q0_1), .a_2(bcd_to_7_segment_5_a_2), .b_2(bcd_to_7_segment_5_b_2),
    .c_2(bcd_to_7_segment_5_c_2), .d_2(bcd_to_7_segment_5_d_2), .e(bcd_to_7_segment_5_e),
    .f(bcd_to_7_segment_5_f), .g(bcd_to_7_segment_5_g));
  or or_4 (or_4_out, and_8_out, and_9_out);
  Clock clock_1 (.out(clock_1_out));
  and and_8 (and_8_out, Q3_0, Q1_0);
  _7_Segment_Display u_7_segment_display_6 (
    .g(bcd_to_7_segment_6_g), .f(bcd_to_7_segment_6_f), .a(bcd_to_7_segment_6_a_2),
    .b(bcd_to_7_segment_6_b_2), .e(bcd_to_7_segment_6_e), .d(bcd_to_7_segment_6_d_2),
    .c(bcd_to_7_segment_6_c_2));  // open: dp
  BCD_to_7_segment bcd_to_7_segment_6 (
    .A(Q3_0), .B(Q2_0), .C(Q1_0), .D(Q0_0), .a_2(bcd_to_7_segment_6_a_2), .b_2(bcd_to_7_segment_6_b_2),
    .c_2(bcd_to_7_segment_6_c_2), .d_2(bcd_to_7_segment_6_d_2), .e(bcd_to_7_segment_6_e),
    .f(bcd_to_7_segment_6_f), .g(bcd_to_7_segment_6_g));
  _4_bit_up_counter u_4_bit_up_counter_6 (
    .Clock(clock_1_out), .CLR(or_4_out), .Preset(Preset_3), .Q3(Q3_0), .Q2(Q2_0), .Q1(Q1_0), .Q0(Q0_0));
  _4_bit_Comparator u_4_bit_comparator_5 (
    .A3(Q3_1), .A2(Q2_1), .A1(Q1_1), .A0(Q0_1), .B3(1'b0), .B2(1'b0), .B1(1'b0), .B0(1'b1),
    .A___B_3(n4_bit_comparator_5_a___b_3));  // open: A___B, A___B_2
  _4_bit_Comparator u_4_bit_comparator_6 (
    .A3(Q3_0), .A2(Q2_0), .A1(Q1_0), .A0(Q0_0), .B3(1'b1), .B2(1'b0), .B1(1'b0), .B0(1'b1),
    .A___B_3(n4_bit_comparator_6_a___b_3));  // open: A___B, A___B_2
  and and_9 (and_9_out, n4_bit_comparator_5_a___b_3, n4_bit_comparator_6_a___b_3);

  // Notes on the sheet:
  //   Hours
  //   Minutes
  //   2107020
  //   2107019
  //   Seconds
endmodule

// 7 Seg. IC
module BCD_to_7_segment (
  input  A,
  input  B,
  input  C,
  input  D,
  output a_2,
  output b_2,
  output c_2,
  output d_2,
  output e,
  output f,
  output g
);

  wire B_prime_C_out, B_prime_D_prime_out, B_XNOR_D_out, BC_prime_D_out, BC_prime_out, BD_prime_out,
       C_prime_D_prime_out, CD_prime_out, CXNORD_out, not_1_out, not_2_out, not_3_out;

  not not_1 (not_1_out, B);
  not not_2 (not_2_out, C);
  not not_3 (not_3_out, D);
  and BC_prime_D (BC_prime_D_out, B, not_2_out, D);
  and B_prime_D_prime (B_prime_D_prime_out, not_1_out, not_3_out);
  and B_prime_C (B_prime_C_out, not_1_out, C);
  and CD_prime (CD_prime_out, C, not_3_out);
  and BD_prime (BD_prime_out, B, not_3_out);
  and BC_prime (BC_prime_out, B, not_2_out);
  and C_prime_D_prime (C_prime_D_prime_out, not_2_out, not_3_out);
  xnor B_XNOR_D (B_XNOR_D_out, B, D);
  xnor CXNORD (CXNORD_out, C, D);
  or A_C_BXNORD (a_2, B_XNOR_D_out, A, C);
  or B_prime_CXnorD (b_2, CXNORD_out, not_1_out);
  or B_C_prime_D (c_2, B, not_2_out, D);
  or A_CD_prime_B_prime_C_B_prime_D_prime_BC_prime_D (d_2, BC_prime_D_out, B_prime_D_prime_out, B_prime_C_out, CD_prime_out, A);
  or CD_prime_B_prime_D_prime (e, B_prime_D_prime_out, CD_prime_out);
  or A_C_prime_D_prime_BC_prime_BD_prime (f, BD_prime_out, BC_prime_out, C_prime_D_prime_out, A);
  or A_BD_prime_BC_prime_B_prime_C (g, B_prime_C_out, BC_prime_out, BD_prime_out, A);

  // Notes on the sheet:
  //   2107019
  //   2107020
endmodule

// Counter
module _4_bit_up_counter (
  input  Clock,
  input  CLR,
  input  Preset,
  output Q3,
  output Q2,
  output Q1,
  output Q0
);

  wire Q0Q1_2_out, Q0Q1_out;

  T_Flip_Flop t_ff_1 (.clk(Clock), .T(1'b1), .Q(Q0), .preset(Preset), .reset(CLR), .en(1'b1));  // open: Qn
  and Q0Q1 (Q0Q1_out, Q0, Q1);
  T_Flip_Flop t_ff_2 (.clk(Clock), .T(Q0), .Q(Q1), .preset(Preset), .reset(CLR), .en(1'b1));  // open: Qn
  T_Flip_Flop t_ff_3 (.clk(Clock), .T(Q0Q1_out), .Q(Q2), .preset(Preset), .reset(CLR), .en(1'b1));  // open: Qn
  and Q0Q1_2 (Q0Q1_2_out, Q0Q1_out, Q2);
  T_Flip_Flop t_ff_4 (.clk(Clock), .T(Q0Q1_2_out), .Q(Q3), .preset(Preset), .reset(CLR), .en(1'b1));  // open: Qn

  // Notes on the sheet:
  //   2107019
  //   2107020
endmodule

// Comparator
module _4_bit_Comparator (
  input  A3,
  input  A2,
  input  A1,
  input  A0,
  input  B3,
  input  B2,
  input  B1,
  input  B0,
  output A___B,
  output A___B_2,
  output A___B_3
);

  wire and_1_out, and_2_out, n2_bit_comparator_1_a___b, n2_bit_comparator_1_a___b_2,
       n2_bit_comparator_1_a___b_3, n2_bit_comparator_2_a___b, n2_bit_comparator_2_a___b_2,
       n2_bit_comparator_2_a___b_3;

  _2_bit_comparator u_2_bit_comparator_1 (
    .A1(A3), .B1(B3), .A0(A2), .B0(B2), .A___B(n2_bit_comparator_1_a___b),
    .A___B_2(n2_bit_comparator_1_a___b_2), .A___B_3(n2_bit_comparator_1_a___b_3));
  _2_bit_comparator u_2_bit_comparator_2 (
    .A1(A1), .B1(B1), .A0(A0), .B0(B0), .A___B(n2_bit_comparator_2_a___b),
    .A___B_2(n2_bit_comparator_2_a___b_2), .A___B_3(n2_bit_comparator_2_a___b_3));
  and and_1 (and_1_out, n2_bit_comparator_1_a___b_3, n2_bit_comparator_2_a___b);
  and and_2 (and_2_out, n2_bit_comparator_1_a___b_3, n2_bit_comparator_2_a___b_2);
  or or_1 (A___B, n2_bit_comparator_1_a___b, and_1_out);
  or or_2 (A___B_2, n2_bit_comparator_1_a___b_2, and_2_out);
  and and_3 (A___B_3, n2_bit_comparator_1_a___b_3, n2_bit_comparator_2_a___b_3);
endmodule

module _1_bit_comparator (
  input  A,
  input  B,
  output A___B,
  output A_B,
  output A___B_2
);

  wire not_1_out, not_2_out;

  not not_1 (not_1_out, A);
  not not_2 (not_2_out, B);
  and and_1 (A___B, not_1_out, B);
  and and_2 (A___B_2, A, not_2_out);
  xnor xnor_1 (A_B, A, B);
endmodule

module _2_bit_comparator (
  input  A1,
  input  B1,
  input  A0,
  input  B0,
  output A___B,
  output A___B_2,
  output A___B_3
);

  wire and_1_out, and_2_out, n1_bit_comparator_1_a___b, n1_bit_comparator_1_a___b_2, n1_bit_comparator_1_a_b,
       n1_bit_comparator_2_a___b, n1_bit_comparator_2_a___b_2, n1_bit_comparator_2_a_b;

  _1_bit_comparator u_1_bit_comparator_1 (
    .A(A1), .B(B1), .A___B(n1_bit_comparator_1_a___b), .A_B(n1_bit_comparator_1_a_b),
    .A___B_2(n1_bit_comparator_1_a___b_2));
  _1_bit_comparator u_1_bit_comparator_2 (
    .A(A0), .B(B0), .A___B(n1_bit_comparator_2_a___b), .A_B(n1_bit_comparator_2_a_b),
    .A___B_2(n1_bit_comparator_2_a___b_2));
  and and_1 (and_1_out, n1_bit_comparator_1_a_b, n1_bit_comparator_2_a___b);
  and and_2 (and_2_out, n1_bit_comparator_1_a_b, n1_bit_comparator_2_a___b_2);
  or or_1 (A___B, n1_bit_comparator_1_a___b, and_1_out);
  or or_2 (A___B_2, n1_bit_comparator_1_a___b_2, and_2_out);
  and and_3 (A___B_3, n1_bit_comparator_1_a_b, n1_bit_comparator_2_a_b);
endmodule
